# Fritzing sketch AssignmentOne (saved by Fritzing 0.9.2b)
breadboards: 2

parts:
  U1 = MAX7219 [package=dil24]
  Part1 = Arduino Uno (Rev3)
  Disp1 = LBT2088AH [part_number=LBT2088AH]
  R1 = Resistor [tolerance=±5% resistance=220 package=THT]
  R2 = Resistor [tolerance=±5% resistance=220 package=THT]

nets:
  N1: U1.DIN, Part1.D11_PWM/MOSI
  N2: U1.DIG4, Disp1.pin1
  GND: U1.GND, U1.GND2, Part1.GND
  N3: U1.DIG6, Disp1.pin2
  N4: U1.DIG2, Disp1.pin_8
  N5: U1.DIG7, Disp1.pin_5
  N6: U1.DIG5, Disp1.pin_7
  N7: U1.LOAD, Part1.D9_PWM
  N8: U1.CLK, Part1.D10_PWM/SS
  N9: U1.SEGA, Disp1.pin_3
  N10: U1.SEGB, Disp1.pin_4
  N11: U1.ISET, R2.Pin_1
  VCC: U1.VCC, Part1.5V, R1.Pin_0
  N12: U1.SEGD, Disp1.pin_6
  N13: R1.Pin_1, R2.Pin_0

notes:
  /**
  * Dokumentation
  *
  *På MAX7219 är SEG DP-SEG G är markerade med grön wire.
  *
  *På MAX7219 är DIG 0-7 är markerade med orange wire.
  *
  *De två resistorerna är på 10K vardera, här skall alltså
  *20K användas totalt. De skall kopplas till pin 18 på MAX7219 *enheten.
  * <--------------------------------------------------------------------->
  * Till Arduino UNO:
  *
  *DIN (pin 1 MAX 7219) kopplas till digital pin 11, lila wire.
  *
  *CLK (pin 13 MAX7219) kopplas till digital pin 10, cyan
  *wire.
  *
  *LOAD (pin 12 MAX7219) kopplas till digital pin 9, rosa wire.
  *
  *V+ (5V) är markerat med röd wire.
  *
  *GND (pin 4, 9 (MAX7219) ) är markerat med svart wire.
