# Fritzing sketch Inlevering2 (saved by Fritzing 0.9.2b)
breadboards: 1

parts:
  Part1 = Arduino Uno (Rev3)
  J1 = Piezo Speaker
  Part2 = TFT 1.8 inch 160x128 w microSD [part_number=358]
  Part3 = Adafruit DS1307 RTC Breakout [part_number="Adafruit #264"]
  R1 = Resistor [tolerance=±5% resistance=220 package=THT]

nets:
  N1: Part1.A1, Part2.LITE
  N2: Part1.A2, Part2.MISO
  N3: Part1.A4/SDA, Part3.SDA
  N4: Part1.A5/SCL, Part3.SCL
  N5: Part1.D8, Part2.CARDCS
  N6: Part1.D9_PWM, Part2.TFTDC
  N7: Part1.D10_PWM/SS, Part2.TFTCS
  N8: Part1.D11_PWM/MOSI, Part2.RESET
  N9: Part1.D12/MISO, Part2.SCLK
  N10: Part1.D13/SCK, Part2.+5V
  GND: Part1.GND, Part2.GND, Part3.GND, R1.Pin_1
  N11: Part1.D3_PWM, J1.pin2
  N12: Part1.D4, Part2.MOSI
  5V: Part1.5V, Part3.VCC
  N13: J1.pin1, R1.Pin_0

custom parts:
  TFT 1.8 inch 160x128 w microSD: This lovely little display breakout is the best way to add a small, colorful and bright display to any project. Since the display uses 4-wire SPI to communicate and has its own pixel-addressable frame buffer, it can be used with every kind of microcontroller. Even a very small one with low memory and few pins available! The 1.8" display has 128x160 color pixels.
  Adafruit DS1307 RTC Breakout: This is a great battery-backed real time clock (RTC) that allows your microcontroller project to keep track of time even if it is reprogrammed, or if the power is lost. Perfect for datalogging, clock-building, time stamping, timers and alarms, etc. The DS1307 is the most popular RTC - but it requires 5V power to work (although we've used it with 5V power and 3.3V logic successfully) PCB &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
