# Fritzing sketch WeatherStationInlev3 (saved by Fritzing 0.9.3b)
breadboards: 1

parts:
  Part1 = Spark Core (v1.0)
  R1 = Photocell (LDR) [package=THT]
  R2 = Resistor [tolerance=±5% resistance=220 package=THT]
  DHT1 = DHT11 Humitidy and Temperature Sensor
  R3 = Resistor [tolerance=±5% resistance=220 package=THT]
  Water_Level_Sensor1 = Water Level Sensor

nets:
  N1: Part1.A3, Water_Level_Sensor1.SIG
  N2: Part1.A5, R1.pin_1, R2.Pin_0
  GND: Part1.GND, R2.Pin_1, DHT1.GND, Water_Level_Sensor1.GND
  N3: Part1.D5, DHT1.DATA, R3.Pin_1
  VDD: Part1.RST, R1.pin_0, DHT1.VDD, R3.Pin_0, Water_Level_Sensor1.VCC

custom parts:
  DHT11 Humitidy and Temperature Sensor: DHT11 Humidity and Temperature Sensor
  Water Level Sensor: A water level sensor. This sensor operates at 3V to 5V. The Sig (signal) pin outputs an analogue signal that is in proportion to the amount of water in contact with the sensor.
